// Logisim project Project.circ as structural Verilog
// control
module controlUnit (
  input  [4:0] opCode,
  input  [1:0] func,
  input  [31:0] A,
  output [1:0] RegDst,
  output RegWr,
  output MemRd,
  output MemWr,
  output ALUSrc,
  output ExtOp,
  output WBdata,
  output [3:0] ALUop,
  output [1:0] PCSrc
);

  wire ADD, ADDI, AND, and_1_out, and_2_out, and_3_out, and_4_out, and_5_out, and_6_out, ANDI, BEQZ, BGEZ,
       BGTZ, BLEZ, BLTZ, BNEZ, CAND, CANDI, comparator_1_eq, comparator_2_eq, comparator_3_eq,
       comparator_4_eq, comparator_5_eq, comparator_6_eq, comparator_7_eq, comparator_8_eq, comparator_10_eq,
       comparator_11_eq, comparator_12_eq, comparator_13_eq, comparator_14_eq, comparator_15_eq,
       comparator_16_eq, comparator_17_eq, decoder_1_out0, decoder_1_out1, EQZ, GTZ, J, JAL, JALR, JR, LTZ,
       LW, NADD, NADDI, OR, or_1_out, or_2_out, or_3_out, or_4_out, or_5_out, or_6_out, or_8_out, or_9_out,
       or_12_out, or_13_out, ORI, R_type, ROR, SET, SLL, SLT, SLTI, SLTU, SLTUI, SRA, SRL, SSET, SW, XOR,
       XORI;
  wire [3:0] multiplexer_1_out, multiplexer_2_out, multiplexer_3_out, multiplexer_4_out, multiplexer_5_out,
       multiplexer_6_out, multiplexer_7_out, multiplexer_8_out, multiplexer_9_out, multiplexer_10_out,
       multiplexer_11_out;

  Decoder #(.select(5), .enable("false")) decoder_1 (
    .out0(decoder_1_out0), .out1(decoder_1_out1), .out4(ANDI), .out5(CANDI), .out6(ORI), .out7(XORI),
    .out8(ADDI), .out9(NADDI), .out10(SLTI), .out11(SLTUI), .out12(SLL), .out13(SRL), .out14(SRA),
    .out15(ROR), .out16(LW), .out17(SW), .out20(BEQZ), .out21(BNEZ), .out22(BLTZ), .out23(BGEZ),
    .out24(BGTZ), .out25(BLEZ), .out26(JR), .out27(JALR), .out28(SET), .out29(SSET), .out30(J), .out31(JAL),
    .sel(opCode));  // open: out2, out3, out18, out19
  Multiplexer #(.width(4), .enable("false")) multiplexer_1 (
    .in0(4'b0000), .in1(4'b0100), .out(multiplexer_1_out), .sel(or_1_out));
  or or_1 (or_1_out, ADD, ADDI);
  or or_2 (or_2_out, EQZ, GTZ);
  or or_3 (or_3_out, EQZ, LTZ);
  Multiplexer #(.width(4), .enable("false")) multiplexer_2 (
    .in0(multiplexer_1_out), .in1(4'b0101), .out(multiplexer_2_out), .sel(or_4_out));
  or or_4 (or_4_out, NADD, NADDI);
  Multiplexer #(.width(4), .enable("false")) multiplexer_3 (
    .in0(multiplexer_2_out), .in1(4'b0110), .out(multiplexer_3_out), .sel(or_5_out));
  or or_5 (or_5_out, SLT, SLTI);
  and and_1 (and_1_out, EQZ, BEQZ);
  and and_2 (and_2_out, ~EQZ, BNEZ);  // AND_Gate
  and and_3 (and_3_out, LTZ, BLTZ);
  and and_4 (and_4_out, or_2_out, BGEZ);
  and and_5 (and_5_out, GTZ, BGTZ);
  and and_6 (and_6_out, or_3_out, BLEZ);
  Comparator #(.width(2), .mode("unsigned")) comparator_1 (.a(func), .b(2'b00), .eq(comparator_1_eq));  // open: gt, lt
  Comparator #(.width(5), .mode("unsigned")) comparator_2 (
    .a(5'b00001), .b(opCode), .eq(comparator_2_eq));  // open: gt, lt
  Comparator #(.width(2), .mode("unsigned")) comparator_3 (.a(func), .b(2'b01), .eq(comparator_3_eq));  // open: gt, lt
  Comparator #(.width(5), .mode("unsigned")) comparator_4 (
    .a(5'b00001), .b(opCode), .eq(comparator_4_eq));  // open: gt, lt
  Comparator #(.width(2), .mode("unsigned")) comparator_5 (.a(func), .b(2'b00), .eq(comparator_5_eq));  // open: gt, lt
  Comparator #(.width(5), .mode("unsigned")) comparator_6 (
    .a({5{1'b0}}), .b(opCode), .eq(comparator_6_eq));  // open: gt, lt
  Comparator #(.width(2), .mode("unsigned")) comparator_7 (.a(func), .b(2'b01), .eq(comparator_7_eq));  // open: gt, lt
  Comparator #(.width(5), .mode("unsigned")) comparator_8 (
    .a({5{1'b0}}), .b(opCode), .eq(comparator_8_eq));  // open: gt, lt
  Multiplexer #(.width(4), .enable("false")) multiplexer_4 (
    .in0(multiplexer_3_out), .in1(4'b0111), .out(multiplexer_4_out), .sel(or_6_out));
  or or_6 (or_6_out, SLTU, SLTUI);
  or or_7 (R_type, decoder_1_out0, decoder_1_out1);
  and and_7 (ADD, comparator_1_eq, comparator_2_eq);
  and and_8 (NADD, comparator_3_eq, comparator_4_eq);
  and and_9 (AND, comparator_5_eq, comparator_6_eq);
  and and_10 (CAND, comparator_7_eq, comparator_8_eq);
  Multiplexer #(.width(4), .enable("false")) multiplexer_5 (
    .in0(multiplexer_4_out), .in1(4'b0000), .out(multiplexer_5_out), .sel(or_8_out));
  or or_8 (or_8_out, OR, ANDI);
  Multiplexer #(.width(4), .enable("false")) multiplexer_6 (
    .in0(multiplexer_5_out), .in1(4'b0001), .out(multiplexer_6_out), .sel(or_9_out));
  or or_9 (or_9_out, CAND, CANDI);
  or or_10 (PCSrc[1], and_1_out, and_2_out, and_3_out, and_4_out, and_5_out, and_6_out);
  Multiplexer #(.width(4), .enable("false")) multiplexer_7 (
    .in0(multiplexer_6_out), .in1(4'b1000), .out(multiplexer_7_out), .sel(SLL));
  Comparator #(.width(32)) comparator_9 (.a(A), .b({32{1'b0}}), .gt(GTZ), .eq(EQZ), .lt(LTZ));
  Multiplexer #(.width(4), .enable("false")) multiplexer_8 (
    .in0(multiplexer_7_out), .in1(4'b1001), .out(multiplexer_8_out), .sel(SRL));
  or or_11 (PCSrc[0], JR, JALR, J, JAL);
  Comparator #(.width(2), .mode("unsigned")) comparator_10 (
    .a(func), .b(2'b10), .eq(comparator_10_eq));  // open: gt, lt
  Comparator #(.width(5), .mode("unsigned")) comparator_11 (
    .a(5'b00001), .b(opCode), .eq(comparator_11_eq));  // open: gt, lt
  Comparator #(.width(2), .mode("unsigned")) comparator_12 (
    .a(func), .b(2'b11), .eq(comparator_12_eq));  // open: gt, lt
  Comparator #(.width(5), .mode("unsigned")) comparator_13 (
    .a(5'b00001), .b(opCode), .eq(comparator_13_eq));  // open: gt, lt
  Comparator #(.width(2), .mode("unsigned")) comparator_14 (
    .a(func), .b(2'b10), .eq(comparator_14_eq));  // open: gt, lt
  Comparator #(.width(5), .mode("unsigned")) comparator_15 (
    .a({5{1'b0}}), .b(opCode), .eq(comparator_15_eq));  // open: gt, lt
  Comparator #(.width(2), .mode("unsigned")) comparator_16 (
    .a(func), .b(2'b11), .eq(comparator_16_eq));  // open: gt, lt
  Comparator #(.width(5), .mode("unsigned")) comparator_17 (
    .a({5{1'b0}}), .b(opCode), .eq(comparator_17_eq));  // open: gt, lt
  Multiplexer #(.width(4), .enable("false")) multiplexer_9 (
    .in0(multiplexer_8_out), .in1(4'b1010), .out(multiplexer_9_out), .sel(SRA));
  ROM #(.addrWidth(5)) rom_1 (.addr(opCode), .data({RegDst, RegWr, ExtOp, ALUSrc, MemRd, MemWr, WBdata}));  // open: sel
  and and_11 (SLT, comparator_10_eq, comparator_11_eq);
  and and_12 (SLTU, comparator_12_eq, comparator_13_eq);
  and and_13 (OR, comparator_14_eq, comparator_15_eq);
  and and_14 (XOR, comparator_16_eq, comparator_17_eq);
  Multiplexer #(.width(4), .enable("false")) multiplexer_10 (
    .in0(multiplexer_9_out), .in1(4'b1011), .out(multiplexer_10_out), .sel(ROR));
  or or_12 (or_12_out, OR, ORI);
  Multiplexer #(.width(4), .enable("false")) multiplexer_11 (
    .in0(multiplexer_10_out), .in1(4'b0011), .out(multiplexer_11_out), .sel(or_12_out));
  or or_13 (or_13_out, XOR, XORI);
  Multiplexer #(.width(4), .enable("false")) multiplexer_12 (
    .in0(multiplexer_11_out), .in1(4'b0100), .out(ALUop), .sel(or_13_out));

  // Other names for the same wires on the sheet: jump = PCSrc[0]; branch = PCSrc[1]

  // Notes on the sheet:
  //   Control Unit:
  //   Main Control:
  //   ALU Control:
  //   inputs
  //   contents of rom_1 (hex, n*v repeats v):
  //   60 60 0 0 8*38 4*28 3d 1a 9*0 a1 e1 e1 0 a1
  //   outputs
  //   PCSrc
endmodule

// alu
module ALU (
  input  [31:0] A,
  input  [31:0] B,
  input  [3:0] ALUop,
  output [31:0] Result
);

  wire and_3_out, and_4_out, comparator_1_lt, comparator_2_lt, NADD, overflow;
  wire [31:0] ADD___NADD, AND, CAND, multiplexer_1_out, negator_1_out, not_1_out, OR, ROR, SLL, SLT, SLTU,
       SRA, SRL, XOR;

  assign not_1_out = ~A;  // NOT_Gate not_1, 32 bits wide
  Negator #(.width(32)) negator_1 (.in(A), .out(negator_1_out));
  assign AND = A & B;  // AND_Gate and_1, 32 bits wide
  assign CAND = not_1_out & B;  // AND_Gate and_2, 32 bits wide
  assign OR = A | B;  // OR_Gate or_1, 32 bits wide
  assign XOR = A ^ B;  // XOR_Gate xor_1, 32 bits wide
  Multiplexer #(.width(32), .enable("false")) multiplexer_1 (
    .in0(A), .in1(negator_1_out), .out(multiplexer_1_out), .sel(NADD));
  and and_3 (and_3_out, ~B[31], ~A[31], ADD___NADD[31], ~NADD);  // AND_Gate
  and and_4 (and_4_out, B[31], A[31], ~ADD___NADD[31], NADD);  // AND_Gate
  Comparator #(.width(32)) comparator_1 (.a(A), .b(B), .lt(comparator_1_lt));  // open: gt, eq
  Comparator #(.width(32), .mode("unsigned")) comparator_2 (.a(A), .b(B), .lt(comparator_2_lt));  // open: gt, eq
  assign SLT = {{31{1'b0}}, comparator_1_lt};  // Bit_Extender bit_extender_1
  assign SLTU = {{31{1'b0}}, comparator_2_lt};  // Bit_Extender bit_extender_2
  Shifter #(.width(32)) shifter_1 (.in(A), .\dist (B[4:0]), .out(SLL));
  Shifter #(.width(32), .shift("lr")) shifter_2 (.in(A), .\dist (B[4:0]), .out(SRL));
  Shifter #(.width(32), .shift("ar")) shifter_3 (.in(A), .\dist (B[4:0]), .out(SRA));
  Shifter #(.width(32), .shift("rr")) shifter_4 (.in(A), .\dist (B[4:0]), .out(ROR));
  Adder #(.width(32)) adder_1 (.a(multiplexer_1_out), .b(B), .out(ADD___NADD), .cin(1'b0));  // open: cout
  or or_2 (overflow, and_3_out, and_4_out);
  Multiplexer #(.select(4), .width(32), .enable("false")) multiplexer_2 (
    .in0(AND), .in1(CAND), .in2(OR), .in3(XOR), .in4(ADD___NADD), .in5(ADD___NADD), .in6(SLT), .in7(SLTU),
    .in8(SLL), .in9(SRL), .in10(SRA), .in11(ROR), .out(Result), .sel(ALUop));  // open: in12, in13, in14, in15
  Comparator #(.width(4), .mode("unsigned")) comparator_3 (.a(4'b0101), .b(ALUop), .eq(NADD));  // open: gt, lt

  // Other names for the same wires on the sheet: shiftAmount[4:0] = B[4:0]

  // Notes on the sheet:
  //   ALU:
  //   ALU operations:
  //   Shift/Rotate Operation:
  //   Logical Operation:
  //   Arthimatic Operation:
  //   Overflow Detection
  //   Set Less Than ( slt / sltu ) :
  //   input:
  //   ALU Multiplexer:
endmodule

// Register File
module RegisterFile (
  input  [2:0] Ra,
  input  [2:0] Rb,
  input  [2:0] Rw,
  input  RegWr,
  input  claer,
  input  [31:0] BusW,
  input  CLK,
  output [31:0] Bus_A,
  output [31:0] Bus_B,
  output [31:0] _0,
  output [31:0] _1,
  output [31:0] _2,
  output [31:0] _3,
  output [31:0] _4,
  output [31:0] _5,
  output [31:0] _6,
  output [31:0] _7
);

  wire and_1_out, and_2_out, and_3_out, and_4_out, and_5_out, and_6_out, and_7_out, and_8_out,
       decoder_1_out0, decoder_1_out1, decoder_1_out2, decoder_1_out3, decoder_1_out4, decoder_1_out5,
       decoder_1_out6, decoder_1_out7, decoder_2_out0, decoder_2_out1, decoder_2_out2, decoder_2_out3,
       decoder_2_out4, decoder_2_out5, decoder_2_out6, decoder_2_out7, decoder_3_out0, decoder_3_out1,
       decoder_3_out2, decoder_3_out3, decoder_3_out4, decoder_3_out5, decoder_3_out6, decoder_3_out7;

  Decoder #(.select(3), .enable("false")) decoder_1 (
    .out0(decoder_1_out0), .out1(decoder_1_out1), .out2(decoder_1_out2), .out3(decoder_1_out3),
    .out4(decoder_1_out4), .out5(decoder_1_out5), .out6(decoder_1_out6), .out7(decoder_1_out7), .sel(Rw));
  and and_1 (and_1_out, decoder_1_out0, RegWr);
  and and_2 (and_2_out, decoder_1_out1, RegWr);
  and and_3 (and_3_out, decoder_1_out2, RegWr);
  and and_4 (and_4_out, decoder_1_out3, RegWr);
  and and_5 (and_5_out, decoder_1_out4, RegWr);
  and and_6 (and_6_out, decoder_1_out5, RegWr);
  and and_7 (and_7_out, decoder_1_out6, RegWr);
  and and_8 (and_8_out, decoder_1_out7, RegWr);
  Register #(.width(32)) R0 (.D(BusW), .en(and_1_out), .Q(_0), .clk(CLK), .clr(claer));
  Register #(.width(32)) R1 (.D(BusW), .en(and_2_out), .Q(_1), .clk(CLK), .clr(claer));
  Register #(.width(32)) R2 (.D(BusW), .en(and_3_out), .Q(_2), .clk(CLK), .clr(claer));
  Register #(.width(32)) R3 (.D(BusW), .en(and_4_out), .Q(_3), .clk(CLK), .clr(claer));
  Register #(.width(32)) R4 (.D(BusW), .en(and_5_out), .Q(_4), .clk(CLK), .clr(claer));
  Register #(.width(32)) R5 (.D(BusW), .en(and_6_out), .Q(_5), .clk(CLK), .clr(claer));
  Register #(.width(32)) R6 (.D(BusW), .en(and_7_out), .Q(_6), .clk(CLK), .clr(claer));
  Register #(.width(32)) R7 (.D(BusW), .en(and_8_out), .Q(_7), .clk(CLK), .clr(claer));
  Decoder #(.select(3), .enable("false")) decoder_2 (
    .out0(decoder_2_out0), .out1(decoder_2_out1), .out2(decoder_2_out2), .out3(decoder_2_out3),
    .out4(decoder_2_out4), .out5(decoder_2_out5), .out6(decoder_2_out6), .out7(decoder_2_out7), .sel(Ra));
  assign Bus_A = decoder_2_out0 ? _0 : 32'bz;  // Controlled_Buffer controlled_buffer_1
  assign Bus_B = decoder_3_out0 ? _0 : 32'bz;  // Controlled_Buffer controlled_buffer_2
  assign Bus_A = decoder_2_out1 ? _1 : 32'bz;  // Controlled_Buffer controlled_buffer_3
  assign Bus_B = decoder_3_out1 ? _1 : 32'bz;  // Controlled_Buffer controlled_buffer_4
  assign Bus_A = decoder_2_out2 ? _2 : 32'bz;  // Controlled_Buffer controlled_buffer_5
  assign Bus_B = decoder_3_out2 ? _2 : 32'bz;  // Controlled_Buffer controlled_buffer_6
  assign Bus_A = decoder_2_out3 ? _3 : 32'bz;  // Controlled_Buffer controlled_buffer_7
  assign Bus_B = decoder_3_out3 ? _3 : 32'bz;  // Controlled_Buffer controlled_buffer_8
  assign Bus_A = decoder_2_out4 ? _4 : 32'bz;  // Controlled_Buffer controlled_buffer_9
  assign Bus_B = decoder_3_out4 ? _4 : 32'bz;  // Controlled_Buffer controlled_buffer_10
  assign Bus_A = decoder_2_out5 ? _5 : 32'bz;  // Controlled_Buffer controlled_buffer_11
  assign Bus_B = decoder_3_out5 ? _5 : 32'bz;  // Controlled_Buffer controlled_buffer_12
  assign Bus_A = decoder_2_out6 ? _6 : 32'bz;  // Controlled_Buffer controlled_buffer_13
  assign Bus_B = decoder_3_out6 ? _6 : 32'bz;  // Controlled_Buffer controlled_buffer_14
  assign Bus_A = decoder_2_out7 ? _7 : 32'bz;  // Controlled_Buffer controlled_buffer_15
  assign Bus_B = decoder_3_out7 ? _7 : 32'bz;  // Controlled_Buffer controlled_buffer_16
  Decoder #(.select(3), .enable("false")) decoder_3 (
    .out0(decoder_3_out0), .out1(decoder_3_out1), .out2(decoder_3_out2), .out3(decoder_3_out3),
    .out4(decoder_3_out4), .out5(decoder_3_out5), .out6(decoder_3_out6), .out7(decoder_3_out7), .sel(Rb));

  // Other names for the same wires on the sheet: A[31:0] = Bus_A; B[31:0] = Bus_B
endmodule

module PCAdress (
  input  CLK,
  input  clear,
  output [31:0] out_3,
  output [31:0] out_4,
  output [31:0] out_5,
  output [31:0] out_6,
  output [31:0] out_7,
  output [31:0] out_8,
  output [31:0] out_9,
  output [31:0] out_10
);

  wire ALUSrc, ExtOp, MemRd, MemWr, RegWr, WBdata;
  wire [1:0] func, PCSrc, RegDst;
  wire [2:0] multiplexer_3_out, Rd, Rs, Rt;
  wire [3:0] ALUop;
  wire [4:0] opCode;
  wire [19:0] BRANCH, imm8_20bit, imm11_20bit, JUMP, multiplexer_1_out, NextPc, register_1_q;
  wire [31:0] A, ALUresult, imm5, imm8, imm11, multiplexer_2_out, Y;

  controlUnit controlunit_1 (
    .opCode(opCode), .func(func), .A(A), .RegDst(RegDst), .RegWr(RegWr), .MemRd(MemRd), .MemWr(MemWr),
    .ALUSrc(ALUSrc), .ExtOp(ExtOp), .WBdata(WBdata), .ALUop(ALUop), .PCSrc(PCSrc));
  Multiplexer #(.select(2), .width(20), .enable("false")) multiplexer_1 (
    .in0(NextPc), .in1(JUMP), .in2(BRANCH), .out(multiplexer_1_out), .sel(PCSrc));  // open: in3
  Register #(.width(20)) register_1 (.D(multiplexer_1_out), .Q(register_1_q), .clk(CLK), .clr(clear));  // open: en
  Multiplexer #(.width(32), .enable("false")) multiplexer_2 (
    .in0(Y), .in1(imm5), .out(multiplexer_2_out), .sel(ALUSrc));
  Adder #(.width(20)) adder_1 (.a(imm11_20bit), .b(register_1_q), .out(JUMP));  // open: cin, cout
  Adder #(.width(20)) adder_2 (.a(imm8_20bit), .b(register_1_q), .out(BRANCH));  // open: cin, cout
  Adder #(.width(20)) adder_3 (.a(20'h1), .b(register_1_q), .out(NextPc));  // open: cin, cout
  ROM #(.addrWidth(20), .dataWidth(16)) rom_1 (.addr(register_1_q), .data({opCode, Rs, Rt, Rd, func}));  // open: sel
  ALU alu_1 (.A(A), .B(multiplexer_2_out), .ALUop(ALUop), .Result(ALUresult));
  // Probe on {opCode, Rs, Rt, Rd, func}
  Extendor extendor_1 (
    .in_1(ExtOp), .in_2({Rd, func}), .in_3({Rt, Rd, func}), .in_4({Rs, Rt, Rd, func}), .OImm5(imm5),
    .OImm8(imm8), .OImm11(imm11), .OImm11_20bit(imm11_20bit), .OImm8_20bit(imm8_20bit));
  Multiplexer #(.select(2), .width(3), .enable("false")) multiplexer_3 (
    .in0(Rt), .in1(Rd), .in2(3'b111), .in3(3'b000), .out(multiplexer_3_out), .sel(RegDst));
  RegisterFile registerfile_1 (
    .Bus_A(A), .Bus_B(Y), ._0(out_3), ._1(out_4), ._2(out_5), ._3(out_6), ._4(out_7), ._5(out_8), ._6(out_9),
    ._7(out_10), .Rw(multiplexer_3_out), .RegWr(RegWr), .BusW(ALUresult), .CLK(CLK), .Ra(Rs), .Rb(Rt),
    .claer(clear));

  // Other names for the same wires on the sheet: _0[31:0] = out_3; _1[31:0] = out_4; _2[31:0] = out_5;
  //   _3[31:0] = out_6; _4[31:0] = out_7; _5[31:0] = out_8; _6[31:0] = out_9; _7[31:0] = out_10; claer = clear;
  //   X[31:0] = A

  // Notes on the sheet:
  //   CONTROL UNIT :
  //   PC Adress and instruction memory:
  //   ALU UNIT :
  //   contents of rom_1 (hex, n*v repeats v):
  //   f002 4244 46ca
  //   ALU UNIT :
  //   INPUT
  //   REGISTERS
endmodule

// Ext
module Extendor (
  input  in_1,
  input  [4:0] in_2,
  input  [7:0] in_3,
  input  [10:0] in_4,
  output [31:0] OImm5,
  output [31:0] OImm8,
  output [31:0] OImm11,
  output [19:0] OImm11_20bit,
  output [19:0] OImm8_20bit
);

  wire multiplexer_1_out, multiplexer_2_out, multiplexer_3_out, multiplexer_4_out, multiplexer_5_out;

  Multiplexer #(.enable("false")) multiplexer_1 (.in0(1'b0), .in1(in_2[4]), .out(multiplexer_1_out), .sel(in_1));
  assign OImm5 = {{27{multiplexer_1_out}}, in_2};  // Bit_Extender bit_extender_1
  Multiplexer #(.enable("false")) multiplexer_2 (.in0(1'b0), .in1(in_3[7]), .out(multiplexer_2_out), .sel(in_1));
  assign OImm8_20bit = {{12{multiplexer_2_out}}, in_3};  // Bit_Extender bit_extender_2
  Multiplexer #(.enable("false")) multiplexer_3 (.in0(1'b0), .in1(in_3[7]), .out(multiplexer_3_out), .sel(in_1));
  assign OImm8 = {{24{multiplexer_3_out}}, in_3};  // Bit_Extender bit_extender_3
  Multiplexer #(.enable("false")) multiplexer_4 (.in0(1'b0), .in1(in_4[10]), .out(multiplexer_4_out), .sel(in_1));
  assign OImm11_20bit = {{9{multiplexer_4_out}}, in_4};  // Bit_Extender bit_extender_4
  Multiplexer #(.enable("false")) multiplexer_5 (.in0(1'b0), .in1(in_4[10]), .out(multiplexer_5_out), .sel(in_1));
  assign OImm11 = {{21{multiplexer_5_out}}, in_4};  // Bit_Extender bit_extender_5

  // Other names for the same wires on the sheet: extOp = in_1; imm5[4:0] = in_2; imm8[7:0] = in_3; imm11[10:0] = in_4

  // Notes on the sheet:
  //   INPUT
  //   OUTPUT
  //   EXTENDOR
endmodule
